// Logisim project singlecycle.circ as structural Verilog: 23 circuits, main circuit main
module main (
  input  in_1
);

  wire alignmentunit_1_cpustall, alignmentunit_1_cpuvalid, alignmentunit_1_memclk, alignmentunit_1_memrd,
       alignmentunit_1_memwr, alignmentunit_1_unalignedread, alignmentunit_1_unalignedwrite, Break_out,
       Clk_out, datamem_1_valid, datamem_2_valid, exeunit_1_boot, exeunit_1_breakon, exeunit_1_dclk,
       exeunit_1_dread, exeunit_1_dwrite, instrmem_1_valid, instrmem_2_valid, keyboard_1_avail,
       lcdctrl_1_lcdclk, lcdctrl_1_lcden, lcdctrl_1_lcdreset, lcdctrl_1_stall, lcdctrl_1_valid,
       memgate2_1_chipclk, memgate2_1_chipwrite, memgate2_1_ledread, memgate2_1_ledwrite,
       memgate2_1_outaddressvalid, memgate2_1_outclk, memgate2_1_outrdrq, memgate2_1_outstall,
       memgate2_1_outwrrq, memgate2_2_chipclk, memgate2_2_chipwrite, memgate2_2_ledread, memgate2_2_ledwrite,
       memgate2_2_outaddressvalid, memgate2_2_outclk, memgate2_2_outrdrq, memgate2_2_outstall,
       memgate2_2_outwrrq, memgate2_3_ledread, memgate2_3_ledwrite, memgate2_3_outaddressvalid,
       memgate2_3_outclk, memgate2_3_outrdrq, memgate2_3_outstall, memgate2_3_outwrrq, memgate2_4_chipclk,
       memgate2_4_chipwrite, memgate2_4_ledread, memgate2_4_ledwrite, memgate2_4_outaddressvalid,
       memgate2_4_outclk, memgate2_4_outrdrq, memgate2_4_outstall, memgate2_4_outwrrq, memgate2_5_chipclk,
       memgate2_5_chipread, memgate2_5_chipwrite, memgate2_5_ledread, memgate2_5_ledwrite,
       memgate2_5_outaddressvalid, memgate2_5_outclk, memgate2_5_outrdrq, memgate2_5_outstall,
       memgate2_5_outwrrq, memgate2_6_chipclk, memgate2_6_chipread, memgate2_6_chipwrite, memgate2_6_ledread,
       memgate2_6_ledwrite, memgate2_6_outaddressvalid, memgate2_6_outrdrq, memgate2_6_outstall,
       memgate2_6_outwrrq, pull_resistor_1_node, pull_resistor_2_node, pull_resistor_3_node,
       pull_resistor_9_node, Resume_out, ttyctrl_1_kbdclk, ttyctrl_1_kbden, ttyctrl_1_kbdreset,
       ttyctrl_1_lcdclk, ttyctrl_1_lcden, ttyctrl_1_lcdreset, ttyctrl_1_stall, ttyctrl_1_valid;
  wire [1:0] exeunit_1_dlen;
  wire [6:0] keyboard_1_data, lcdctrl_1_xcoord, lcdctrl_1_ycoord, ttyctrl_1_lcdchar;
  wire [23:0] lcdctrl_1_pix;
  wire [31:0] alignmentunit_1_cpurddata, alignmentunit_1_memaddr, alignmentunit_1_memwrdata,
       datamem_1_rddata, datamem_2_rddata, exeunit_1_daddr, exeunit_1_dwrdata, exeunit_1_iaddr,
       instrmem_1_data, instrmem_2_data, lcdctrl_1_rddata, memgate2_1_chipaddr, memgate2_1_chipwrdata,
       memgate2_1_outaddr, memgate2_1_outreaddata, memgate2_1_outwrdata, memgate2_2_chipaddr,
       memgate2_2_chipwrdata, memgate2_2_outaddr, memgate2_2_outreaddata, memgate2_2_outwrdata,
       memgate2_3_chipaddr, memgate2_3_outaddr, memgate2_3_outreaddata, memgate2_3_outwrdata,
       memgate2_4_chipwrdata, memgate2_4_outaddr, memgate2_4_outreaddata, memgate2_4_outwrdata,
       memgate2_5_chipaddr, memgate2_5_chipwrdata, memgate2_5_outaddr, memgate2_5_outreaddata,
       memgate2_5_outwrdata, memgate2_6_chipaddr, memgate2_6_chipwrdata, memgate2_6_outaddr,
       memgate2_6_outreaddata, memgate2_6_outwrdata, pull_resistor_8_node, register_1_q, ttyctrl_1_rddata;

  LED Stopped (.in(exeunit_1_breakon));
  Button Break (.out(Break_out));
  Button Resume (.out(Resume_out));
  Clock Clk (.out(Clk_out));
  LED Booting (.in(exeunit_1_boot));
  DotMatrix #(.matrixcols(32), .matrixrows(1)) dotmatrix_1 (
    .col0(register_1_q[31]), .col1(register_1_q[30]), .col2(register_1_q[29]), .col3(register_1_q[28]),
    .col4(register_1_q[27]), .col5(register_1_q[26]), .col6(register_1_q[25]), .col7(register_1_q[24]),
    .col8(register_1_q[23]), .col9(register_1_q[22]), .col10(register_1_q[21]), .col11(register_1_q[20]),
    .col12(register_1_q[19]), .col13(register_1_q[18]), .col14(register_1_q[17]), .col15(register_1_q[16]),
    .col16(register_1_q[15]), .col17(register_1_q[14]), .col18(register_1_q[13]), .col19(register_1_q[12]),
    .col20(register_1_q[11]), .col21(register_1_q[10]), .col22(register_1_q[9]), .col23(register_1_q[8]),
    .col24(register_1_q[7]), .col25(register_1_q[6]), .col26(register_1_q[5]), .col27(register_1_q[4]),
    .col28(register_1_q[3]), .col29(register_1_q[2]), .col30(register_1_q[1]), .col31(register_1_q[0]));
  ExeUnit exeunit_1 (
    .DClk(exeunit_1_dclk), .DRead(exeunit_1_dread), .DWrite(exeunit_1_dwrite), .DAddr(exeunit_1_daddr),
    .DWrData(exeunit_1_dwrdata), .DLen(exeunit_1_dlen), .Boot(exeunit_1_boot), .BreakOn(exeunit_1_breakon),
    .IAddr(exeunit_1_iaddr), .DData(alignmentunit_1_cpurddata), .DValid(alignmentunit_1_cpuvalid),
    .DStall(alignmentunit_1_cpustall), .ClkIn(Clk_out), .DoBreak(Break_out), .DoResume(Resume_out),
    .IValid(instrmem_1_valid), .IData(instrmem_1_data));
  // Probe on register_1_q
  // Probe on exeunit_1_iaddr
  AlignmentUnit alignmentunit_1 (
    .MemClk(alignmentunit_1_memclk), .MemRd(alignmentunit_1_memrd), .MemWr(alignmentunit_1_memwr),
    .MemAddr(alignmentunit_1_memaddr), .MemWrData(alignmentunit_1_memwrdata),
    .CpuRdData(alignmentunit_1_cpurddata), .CpuValid(alignmentunit_1_cpuvalid),
    .CpuStall(alignmentunit_1_cpustall), .UnalignedRead(alignmentunit_1_unalignedread),
    .UnalignedWrite(alignmentunit_1_unalignedwrite), .MemRdData(memgate2_1_outreaddata),
    .MemValid(memgate2_1_outaddressvalid), .MemStall(memgate2_1_outstall), .CpuClk(exeunit_1_dclk),
    .CpuRd(exeunit_1_dread), .CpuWr(exeunit_1_dwrite), .CpuAddr(exeunit_1_daddr),
    .CpuWrData(exeunit_1_dwrdata), .CpuLen(exeunit_1_dlen));
  LED led_1 (.in(alignmentunit_1_unalignedread));
  LED led_2 (.in(alignmentunit_1_unalignedwrite));
  InstrMem instrmem_1 (.Data(instrmem_1_data), .Valid(instrmem_1_valid), .Address(exeunit_1_iaddr));
  LED led_3 (.in(memgate2_1_ledread));
  LED led_4 (.in(memgate2_1_ledwrite));
  MemGate2 memgate2_1 (
    .OutReadData(memgate2_1_outreaddata), .OutAddressValid(memgate2_1_outaddressvalid),
    .OutStall(memgate2_1_outstall), .ChipAddr(memgate2_1_chipaddr), .LedRead(memgate2_1_ledread),
    .LedWrite(memgate2_1_ledwrite), .ChipWrite(memgate2_1_chipwrite), .ChipClk(memgate2_1_chipclk),
    .OutRdRq(memgate2_1_outrdrq), .OutWrRq(memgate2_1_outwrrq), .OutAddr(memgate2_1_outaddr),
    .OutWrData(memgate2_1_outwrdata), .OutClk(memgate2_1_outclk), .ChipWrData(memgate2_1_chipwrdata),
    .ParamLen(32'h40000), .ParamSub(1'b1), .InRdRq(alignmentunit_1_memrd), .InWrRq(alignmentunit_1_memwr),
    .InAddr(alignmentunit_1_memaddr), .InWrData(alignmentunit_1_memwrdata), .InClk(alignmentunit_1_memclk),
    .ChipValid(datamem_1_valid), .ChipRdData(datamem_1_rddata), .ParamBase({32{1'b0}}),
    .InReadData(memgate2_2_outreaddata), .InAddressValid(memgate2_2_outaddressvalid),
    .InStall(memgate2_2_outstall));  // open: ChipRead, ChipStall
  DataMem datamem_1 (
    .RdData(datamem_1_rddata), .Valid(datamem_1_valid), .Addr(memgate2_1_chipaddr),
    .WrData(memgate2_1_chipwrdata), .WrEn(memgate2_1_chipwrite), .Clk(memgate2_1_chipclk));
  LED led_5 (.in(memgate2_2_ledread));
  DataMem datamem_2 (
    .RdData(datamem_2_rddata), .Valid(datamem_2_valid), .Addr(memgate2_2_chipaddr),
    .WrData(memgate2_2_chipwrdata), .WrEn(memgate2_2_chipwrite), .Clk(memgate2_2_chipclk));
  LED led_6 (.in(memgate2_2_ledwrite));
  MemGate2 memgate2_2 (
    .OutReadData(memgate2_2_outreaddata), .OutAddressValid(memgate2_2_outaddressvalid),
    .OutStall(memgate2_2_outstall), .ChipAddr(memgate2_2_chipaddr), .LedRead(memgate2_2_ledread),
    .LedWrite(memgate2_2_ledwrite), .ChipWrite(memgate2_2_chipwrite), .ChipClk(memgate2_2_chipclk),
    .OutRdRq(memgate2_2_outrdrq), .OutWrRq(memgate2_2_outwrrq), .OutAddr(memgate2_2_outaddr),
    .OutWrData(memgate2_2_outwrdata), .OutClk(memgate2_2_outclk), .ChipWrData(memgate2_2_chipwrdata),
    .ParamLen(32'h40000), .ParamSub(1'b1), .InRdRq(memgate2_1_outrdrq), .InWrRq(memgate2_1_outwrrq),
    .InAddr(memgate2_1_outaddr), .InWrData(memgate2_1_outwrdata), .InClk(memgate2_1_outclk),
    .ChipValid(datamem_2_valid), .ChipRdData(datamem_2_rddata), .ParamBase(32'h40000),
    .InReadData(memgate2_3_outreaddata), .InAddressValid(memgate2_3_outaddressvalid),
    .InStall(memgate2_3_outstall));  // open: ChipRead, ChipStall
  LED led_7 (.in(memgate2_3_ledread));
  LED led_8 (.in(memgate2_3_ledwrite));
  MemGate2 memgate2_3 (
    .OutReadData(memgate2_3_outreaddata), .OutAddressValid(memgate2_3_outaddressvalid),
    .OutStall(memgate2_3_outstall), .ChipAddr(memgate2_3_chipaddr), .LedRead(memgate2_3_ledread),
    .LedWrite(memgate2_3_ledwrite), .OutRdRq(memgate2_3_outrdrq), .OutWrRq(memgate2_3_outwrrq),
    .OutAddr(memgate2_3_outaddr), .OutWrData(memgate2_3_outwrdata), .OutClk(memgate2_3_outclk),
    .ParamLen(32'h40000), .ParamSub(1'b0), .InRdRq(memgate2_2_outrdrq), .InWrRq(memgate2_2_outwrrq),
    .InAddr(memgate2_2_outaddr), .InWrData(memgate2_2_outwrdata), .InClk(memgate2_2_outclk),
    .ChipValid(instrmem_2_valid), .ChipRdData(instrmem_2_data), .ParamBase(32'h80020000),
    .InReadData(memgate2_4_outreaddata), .InAddressValid(memgate2_4_outaddressvalid),
    .InStall(memgate2_4_outstall));  // open: ChipRead, ChipWrite, ChipClk, ChipWrData, ChipStall
  InstrMem instrmem_2 (.Data(instrmem_2_data), .Valid(instrmem_2_valid), .Address(memgate2_3_chipaddr));
  LED led_9 (.in(memgate2_4_ledread));
  LED led_10 (.in(memgate2_4_ledwrite));
  Pull_Resistor pull_resistor_1 (.node(pull_resistor_1_node));
  Pull_Resistor #(.pull(1)) pull_resistor_2 (.node(pull_resistor_2_node));
  MemGate2 memgate2_4 (
    .OutReadData(memgate2_4_outreaddata), .OutAddressValid(memgate2_4_outaddressvalid),
    .OutStall(memgate2_4_outstall), .LedRead(memgate2_4_ledread), .LedWrite(memgate2_4_ledwrite),
    .ChipWrite(memgate2_4_chipwrite), .ChipClk(memgate2_4_chipclk), .OutRdRq(memgate2_4_outrdrq),
    .OutWrRq(memgate2_4_outwrrq), .OutAddr(memgate2_4_outaddr), .OutWrData(memgate2_4_outwrdata),
    .OutClk(memgate2_4_outclk), .ChipWrData(memgate2_4_chipwrdata), .ParamLen(32'h4), .ParamSub(1'b1),
    .InRdRq(memgate2_3_outrdrq), .InWrRq(memgate2_3_outwrrq), .InAddr(memgate2_3_outaddr),
    .InWrData(memgate2_3_outwrdata), .InClk(memgate2_3_outclk), .ChipStall(pull_resistor_1_node),
    .ChipValid(pull_resistor_2_node), .ChipRdData(register_1_q), .ParamBase(32'hf0000000),
    .InReadData(memgate2_5_outreaddata), .InAddressValid(memgate2_5_outaddressvalid),
    .InStall(memgate2_5_outstall));  // open: ChipAddr, ChipRead
  TtyCtrl ttyctrl_1 (
    .KbdClk(ttyctrl_1_kbdclk), .KbdEn(ttyctrl_1_kbden), .Stall(ttyctrl_1_stall),
    .KbdReset(ttyctrl_1_kbdreset), .Valid(ttyctrl_1_valid), .RdData(ttyctrl_1_rddata),
    .LcdChar(ttyctrl_1_lcdchar), .LcdClk(ttyctrl_1_lcdclk), .LcdReset(ttyctrl_1_lcdreset),
    .LcdEn(ttyctrl_1_lcden), .Addr(memgate2_5_chipaddr), .Rd(memgate2_5_chipread), .Wr(memgate2_5_chipwrite),
    .Clk(memgate2_5_chipclk), .KbdAvail(keyboard_1_avail), .KbdChar(keyboard_1_data),
    .WrData(memgate2_5_chipwrdata));
  Register #(.width(32)) register_1 (
    .D(memgate2_4_chipwrdata), .en(memgate2_4_chipwrite), .Q(register_1_q), .clk(memgate2_4_chipclk));  // open: clr
  LED led_11 (.in(memgate2_5_ledread));
  LED led_12 (.in(memgate2_5_ledwrite));
  MemGate2 memgate2_5 (
    .OutReadData(memgate2_5_outreaddata), .OutAddressValid(memgate2_5_outaddressvalid),
    .OutStall(memgate2_5_outstall), .ChipAddr(memgate2_5_chipaddr), .LedRead(memgate2_5_ledread),
    .ChipRead(memgate2_5_chipread), .LedWrite(memgate2_5_ledwrite), .ChipWrite(memgate2_5_chipwrite),
    .ChipClk(memgate2_5_chipclk), .OutRdRq(memgate2_5_outrdrq), .OutWrRq(memgate2_5_outwrrq),
    .OutAddr(memgate2_5_outaddr), .OutWrData(memgate2_5_outwrdata), .OutClk(memgate2_5_outclk),
    .ChipWrData(memgate2_5_chipwrdata), .ParamLen(32'hc), .ParamSub(1'b1), .InRdRq(memgate2_4_outrdrq),
    .InWrRq(memgate2_4_outwrrq), .InAddr(memgate2_4_outaddr), .InWrData(memgate2_4_outwrdata),
    .InClk(memgate2_4_outclk), .ChipStall(ttyctrl_1_stall), .ChipValid(ttyctrl_1_valid),
    .ChipRdData(ttyctrl_1_rddata), .ParamBase(32'hf0000004), .InReadData(memgate2_6_outreaddata),
    .InAddressValid(memgate2_6_outaddressvalid), .InStall(memgate2_6_outstall));
  TTY tty_1 (.data(ttyctrl_1_lcdchar), .clk(ttyctrl_1_lcdclk), .we(ttyctrl_1_lcden), .clr(ttyctrl_1_lcdreset));
  LED led_13 (.in(memgate2_6_ledread));
  LcdCtrl lcdctrl_1 (
    .Stall(lcdctrl_1_stall), .Valid(lcdctrl_1_valid), .RdData(lcdctrl_1_rddata), .Xcoord(lcdctrl_1_xcoord),
    .Ycoord(lcdctrl_1_ycoord), .Pix(lcdctrl_1_pix), .LcdClk(lcdctrl_1_lcdclk), .LcdEn(lcdctrl_1_lcden),
    .LcdReset(lcdctrl_1_lcdreset), .Addr(memgate2_6_chipaddr), .Rd(memgate2_6_chipread),
    .Wr(memgate2_6_chipwrite), .Clk(memgate2_6_chipclk), .WrData(memgate2_6_chipwrdata));
  Keyboard keyboard_1 (
    .clk(ttyctrl_1_kbdclk), .re(ttyctrl_1_kbden), .clr(ttyctrl_1_kbdreset), .avail(keyboard_1_avail),
    .data(keyboard_1_data));
  // RGB_Video #(.cursor("No Cursor")) rgb_video_1: pin names not known; wires that end beside it: lcdctrl_1_lcdreset, lcdctrl_1_lcdclk, lcdctrl_1_lcden, lcdctrl_1_xcoord, lcdctrl_1_ycoord, lcdctrl_1_pix
  LED led_14 (.in(memgate2_6_ledwrite));
  Pull_Resistor pull_resistor_3 (.node(pull_resistor_3_node));
  MemGate2 memgate2_6 (
    .OutReadData(memgate2_6_outreaddata), .OutAddressValid(memgate2_6_outaddressvalid),
    .OutStall(memgate2_6_outstall), .ChipAddr(memgate2_6_chipaddr), .LedRead(memgate2_6_ledread),
    .ChipRead(memgate2_6_chipread), .LedWrite(memgate2_6_ledwrite), .ChipWrite(memgate2_6_chipwrite),
    .ChipClk(memgate2_6_chipclk), .OutRdRq(memgate2_6_outrdrq), .OutWrRq(memgate2_6_outwrrq),
    .OutAddr(memgate2_6_outaddr), .OutWrData(memgate2_6_outwrdata), .OutClk(pull_resistor_3_node),
    .ChipWrData(memgate2_6_chipwrdata), .ParamLen(32'h10004), .ParamSub(1'b1), .InRdRq(memgate2_5_outrdrq),
    .InWrRq(memgate2_5_outwrrq), .InAddr(memgate2_5_outaddr), .InWrData(memgate2_5_outwrdata),
    .InClk(memgate2_5_outclk), .ChipStall(lcdctrl_1_stall), .ChipValid(lcdctrl_1_valid),
    .ChipRdData(lcdctrl_1_rddata), .ParamBase(32'hf0000010), .InReadData(pull_resistor_8_node),
    .InAddressValid(pull_resistor_9_node), .InStall(in_1));
  Pull_Resistor pull_resistor_4 (.node(memgate2_6_outrdrq));
  Pull_Resistor pull_resistor_5 (.node(memgate2_6_outwrrq));
  Pull_Resistor pull_resistor_6 (.node(memgate2_6_outaddr));
  Pull_Resistor pull_resistor_7 (.node(memgate2_6_outwrdata));
  Pull_Resistor pull_resistor_8 (.node(pull_resistor_8_node));
  Pull_Resistor pull_resistor_9 (.node(pull_resistor_9_node));

  // Notes on the sheet:
  //   data
  //   data 2
  //   rom
  //   led line
  //   tty/serial
  //   display
endmodule

module InstrMem (
  input  [31:0] Address,
  output [31:0] Data,
  output Valid
);

  wire comparator_1_gt, comparator_2_lt, transmission_1_p2;
  wire [31:0] rom_1_data, subtractor_1_out;

  Subtractor #(.width(32)) subtractor_1 (.a(Address), .b(32'h8001ffff), .out(subtractor_1_out));  // open: bin, bout
  Comparator #(.mode("unsigned"), .width(32)) comparator_1 (
    .a(Address), .b(32'h8001ffff), .gt(comparator_1_gt));  // open: eq, lt
  Comparator #(.mode("unsigned"), .width(32)) comparator_2 (
    .a(subtractor_1_out), .b(32'h40000), .lt(comparator_2_lt));  // open: gt, eq
  ROM #(.addrWidth(16), .dataWidth(32)) rom_1 (.addr(subtractor_1_out[17:2]), .data(rom_1_data));
  and and_1 (Valid, comparator_2_lt, comparator_1_gt);
  // Transmission_Gate #(.width(32)) transmission_1: pin names not known; wires that end beside it: rom_1_data, transmission_1_p2, Valid, Data
  not not_1 (transmission_1_p2, Valid);

  // Notes on the sheet:
  //   Address: pull=down
  //   Valid: pull=down
  //   contents of rom_1 (hex, n*v repeats v):
  //   3c10f000 2408ffff ae080000 3c1d0000 27bd2000 3c1c0000 279c7ff0 3a0f025 3c080000 25080000 3c090000
  //   25290000 11090004 0 ad000000 1509fffe 21080004 3c080000 25080000 3c090000 25290000 3c0a8002 254a05ac
  //   11090006 0 8d4b0000 ad0b0000 214a0004 1509fffc 21080004 24040000 24050000 ae040000 c00803e 0 d
  //   1000fffe 0 f0010f30 5*0 10000 3000001 4*0 80020000 7*0 f41 756e6700 70100 3040000 3c02f000 24080006
  //   ac400000 ac480004 24080001 ac480010 2407006c 24060065 24080048 ac48000c 3c0300ff ac46000c ac47000c
  //   ac47000c 2407006f 3463ffff ac47000c 2405000a 24070021 ac47000c ac45000c ac430014 ac430018 ac43001c
  //   ac430020 ac430024 ac430028 ac43002c ac430030 ac430034 ac430038 ac43003c ac430040 ac430044 ac430048
  //   ac43004c ac430050 ac430214 ac430218 ac43021c ac430220 ac430224 ac430228 ac43022c ac430230 ac430234
  //   ac430238 ac43023c ac430240 ac430244 ac430248 ac43024c ac430250 ac430414 ac430418 ac43041c ac430420
  //   ac430424 ac430428 ac43042c ac430430 ac430434 ac430438 ac43043c ac430440 ac430444 ac430448 ac43044c
  //   ac430450 ac430614 ac430618 ac43061c ac430620 ac430624 ac430628 ac43062c ac430630 ac430634 ac430638
  //   ac43063c ac430640 ac430644 ac430648 ac43064c ac430650 ac430814 ac430818 ac43081c ac430820 ac430824
  //   ac430828 ac43082c ac430830 ac430834 ac430838 ac43083c ac430840 ac430844 ac430848 ac43084c ac430850
  //   ac430a14 ac430a18 ac430a1c ac430a20 ac430a24 ac430a28 ac430a2c ac430a30 ac430a34 ac430a38 ac430a3c
  //   ac430a40 ac430a44 ac430a48 ac430a4c ac430a50 ac430c14 ac430c18 ac430c1c ac430c20 ac430c24 ac430c28
  //   ac430c2c ac430c30 ac430c34 ac430c38 ac430c3c ac430c40 ac430c44 ac430c48 ac430c4c ac430c50 ac430e14
  //   ac430e18 ac430e1c ac430e20 ac430e24 ac430e28 ac430e2c ac430e30 ac430e34 ac430e38 ac430e3c ac430e40
  //   ac430e44 ac430e48 ac430e4c ac430e50 ac431014 ac431018 ac43101c ac431020 ac431024 ac431028 ac43102c
  //   ac431030 ac431034 ac431038 ac43103c ac431040 ac431044 ac431048 ac43104c ac431050 ac431214 ac431218
  //   ac43121c ac431220 ac431224 ac431228 ac43122c ac431230 ac431234 ac431238 ac43123c ac431240 ac431244
  //   ac431248 ac43124c ac431250 ac431414 ac431418 ac43141c ac431420 ac431424 ac431428 ac43142c ac431430
  //   ac431434 ac431438 ac43143c ac431440 ac431444 ac431448 ac43144c ac431450 ac431614 ac431618 ac43161c
  //   ac431620 ac431624 ac431628 ac43162c ac431630 ac431634 ac431638 ac43163c ac431640 ac431644 ac431648
  //   ac43164c ac431650 ac431814 ac431818 ac43181c ac431820 ac431824 ac431828 ac43182c ac431830 ac431834
  //   ac431838 ac43183c ac431840 ac431844 ac431848 ac43184c ac431850 ac431a14 ac431a18 ac431a1c ac431a20
  //   ac431a24 ac431a28 ac431a2c ac431a30 ac431a34 ac431a38 ac431a3c ac431a40 ac431a44 ac431a48 ac431a4c
  //   ac431a50 ac431c14 ac431c18 ac431c1c ac431c20 ac431c24 ac431c28 ac431c2c ac431c30 ac431c34 ac431c38
  //   ac431c3c ac431c40 ac431c44 ac431c48 ac431c4c ac431c50 ac431e14 ac431e18 ac431e1c ac431e20 ac431e24
  //   ac431e28 ac431e2c ac431e30 ac431e34 ac431e38 ac431e3c ac431e40 ac431e44 ac431e48 ac431e4c ac431e50
  //   24030079 ac43000c 24030061 ac46000c ac43000c 24030068 ac43000c 3c04f000 ac45000c 8c820004 0 30420001
  //   1040fffc 0 8c820008 0 ac82000c 8c820004 0 30420001 1040fff4 0 1000fff7
endmodule

module DataMem (
  input  WrEn,
  input  Clk,
  input  [31:0] Addr,
  input  [31:0] WrData,
  output [31:0] RdData,
  output Valid
);

  wire and_1_out;

  Comparator #(.width(14)) comparator_1 (.a(Addr[31:18]), .b({14{1'b0}}), .eq(Valid));  // open: gt, lt
  RAM #(.addrWidth(16), .asyncread("true"), .dataWidth(32)) cpu_ram (
    .addr(Addr[17:2]), .we(and_1_out), .oe(Valid), .clk(Clk), .din(WrData), .dout(RdData));
  and and_1 (and_1_out, WrEn, Valid);
  Pull_Resistor pull_resistor_1 (.node(RdData));
endmodule

module ALU (
  input  shamt_reg,
  input  [31:0] A,
  input  [4:0] control,
  input  [31:0] B,
  input  [4:0] shamt,
  input  mulclk,
  output [31:0] out_7
);

  wire and_1_out, comparator_1_lt, not_1_out, subtractor_1_bout;
  wire [0:0] comparator_2_lt, comparator_3_lt;
  wire [2:0] bit_extender_2_out;
  wire [4:0] bit_extender_1_out, multiplexer_1_out, multiplexer_2_out, subtractor_1_out;
  wire [31:0] adder_1_out, and_2_out, divider_1_out, divider_1_rem, divider_2_out, divider_2_rem,
       multiplexer_3_out, multiplexer_4_out, multiplier_1_cout, multiplier_1_out, multiplier_2_cout,
       multiplier_2_out, nor_1_out, or_1_out, pull_resistor_1_node, pull_resistor_2_node,
       pull_resistor_3_node, pull_resistor_4_node, pull_resistor_5_node, pull_resistor_6_node,
       pull_resistor_7_node, pull_resistor_8_node, pull_resistor_9_node, pull_resistor_10_node,
       pull_resistor_11_node, pull_resistor_12_node, pull_resistor_13_node, pull_resistor_14_node,
       pull_resistor_15_node, pull_resistor_16_node, pull_resistor_17_node, register_1_q, register_2_q,
       shifter_1_out, shifter_2_out, shifter_3_out, shifter_4_out, subtractor_2_out, xor_1_out;
  wire [63:0] multiplexer_5_out;

  Subtractor #(.width(5)) subtractor_1 (
    .a(control), .b(5'b01101), .out(subtractor_1_out), .bout(subtractor_1_bout));  // open: bin
  not not_1 (not_1_out, subtractor_1_bout);
  Multiplexer #(.enable("false"), .width(5)) multiplexer_1 (
    .in0(shamt), .in1(bit_extender_1_out), .out(multiplexer_1_out), .sel(shamt_reg));
  Bit_Extender #(.in_width(32), .out_width(5), .\type ("zero")) bit_extender_1 (.in(B), .out(bit_extender_1_out));
  Bit_Extender #(.in_width(5), .out_width(3)) bit_extender_2 (.in(subtractor_1_out), .out(bit_extender_2_out));
  Comparator #(.mode("unsigned"), .width(5)) comparator_1 (
    .a(subtractor_1_out), .b(5'b01000), .lt(comparator_1_lt));  // open: gt, eq
  and and_1 (and_1_out, comparator_1_lt, not_1_out);
  Multiplexer #(.select(3), .width(5)) multiplexer_2 (
    .in0({5{1'b0}}), .in1({5{1'b0}}), .in2(5'b01100), .in3(5'b10100), .in4(5'b11000), .in5(5'b11001),
    .in6(5'b11010), .in7(5'b11011), .out(multiplexer_2_out));  // open: sel, en
  Adder #(.width(32)) adder_1 (.a(A), .b(B), .out(adder_1_out));  // open: cin, cout
  Subtractor #(.width(32)) subtractor_2 (.a(A), .b(B), .out(subtractor_2_out));  // open: bin, bout
  Comparator #(.width(32)) comparator_2 (.a(A), .b(B), .lt(comparator_2_lt[0]));  // open: gt, eq
  Comparator #(.mode("unsigned"), .width(32)) comparator_3 (.a(A), .b(B), .lt(comparator_3_lt[0]));  // open: gt, eq
  assign and_2_out = A & B;  // AND_Gate and_2, 32 bits wide
  assign or_1_out = A | B;  // OR_Gate or_1, 32 bits wide
  assign xor_1_out = A ^ B;  // XOR_Gate xor_1, 32 bits wide
  assign nor_1_out = ~(A | B);  // NOR_Gate nor_1, 32 bits wide
  Shifter #(.width(32)) shifter_1 (.in(A), .\dist (multiplexer_1_out), .out(shifter_1_out));
  Shifter #(.shift("lr"), .width(32)) shifter_2 (.in(A), .\dist (multiplexer_1_out), .out(shifter_2_out));
  Shifter #(.shift("ar"), .width(32)) shifter_3 (.in(A), .\dist (multiplexer_1_out), .out(shifter_3_out));
  Shifter #(.width(32)) shifter_4 (.in(B), .\dist (5'b10000), .out(shifter_4_out));
  Multiplier #(.mode("twosComplement"), .width(32)) multiplier_1 (
    .a(A), .b(B), .out(multiplier_1_out), .cout(multiplier_1_cout));  // open: cin
  Multiplier #(.width(32)) multiplier_2 (.a(A), .b(B), .out(multiplier_2_out), .cout(multiplier_2_cout));  // open: cin
  Divider #(.mode("twosComplement"), .width(32)) divider_1 (
    .a(A), .b(B), .out(divider_1_out), .rem(divider_1_rem));  // open: upper
  Divider #(.width(32)) divider_2 (.a(A), .b(B), .out(divider_2_out), .rem(divider_2_rem));  // open: upper
  Multiplexer #(.enable("false"), .select(2), .width(32)) multiplexer_3 (
    .in0(multiplier_1_out), .in1(multiplier_2_out), .in2(divider_1_out), .in3(divider_2_out),
    .out(multiplexer_3_out), .sel(multiplexer_2_out[1:0]));
  Multiplexer #(.enable("false"), .select(2), .width(32)) multiplexer_4 (
    .in0(multiplier_1_cout), .in1(multiplier_2_cout), .in2(divider_1_rem), .in3(divider_2_rem),
    .out(multiplexer_4_out));  // open: sel
  Multiplexer #(.enable("false"), .width(64)) multiplexer_5 (
    .in0({multiplexer_4_out, multiplexer_3_out}), .in1({A, A}), .out(multiplexer_5_out),
    .sel(multiplexer_2_out[2]));
  Pull_Resistor pull_resistor_1 (.node(pull_resistor_1_node));
  Pull_Resistor pull_resistor_2 (.node(pull_resistor_2_node));
  Pull_Resistor pull_resistor_3 (.node(pull_resistor_3_node));
  Pull_Resistor pull_resistor_4 (.node(pull_resistor_4_node));
  Pull_Resistor pull_resistor_5 (.node(pull_resistor_5_node));
  Pull_Resistor pull_resistor_6 (.node(pull_resistor_6_node));
  Pull_Resistor #(.pull("X")) pull_resistor_7 (.node(pull_resistor_7_node));
  Pull_Resistor #(.pull("X")) pull_resistor_8 (.node(pull_resistor_8_node));
  Pull_Resistor #(.pull("X")) pull_resistor_9 (.node(pull_resistor_9_node));
  Pull_Resistor #(.pull("X")) pull_resistor_10 (.node(pull_resistor_10_node));
  Pull_Resistor #(.pull("X")) pull_resistor_11 (.node(pull_resistor_11_node));
  Pull_Resistor #(.pull("X")) pull_resistor_12 (.node(pull_resistor_12_node));
  Pull_Resistor #(.pull("X")) pull_resistor_13 (.node(pull_resistor_13_node));
  Pull_Resistor #(.pull("X")) pull_resistor_14 (.node(pull_resistor_14_node));
  Pull_Resistor #(.pull("X")) pull_resistor_15 (.node(pull_resistor_15_node));
  Pull_Resistor #(.pull("X")) pull_resistor_16 (.node(pull_resistor_16_node));
  Pull_Resistor pull_resistor_17 (.node(pull_resistor_17_node));
  Multiplexer #(.enable("false"), .select(5), .width(32)) multiplexer_6 (
    .in0(adder_1_out), .in1(subtractor_2_out), .in2({{31{1'b0}}, comparator_2_lt[0]}),
    .in3({{31{1'b0}}, comparator_3_lt[0]}), .in4(and_2_out), .in5(or_1_out), .in6(xor_1_out),
    .in7(nor_1_out), .in8(shifter_1_out), .in9(shifter_2_out), .in10(shifter_3_out), .in11(shifter_4_out),
    .in12(B), .in13(register_1_q), .in14(register_2_q), .in15(pull_resistor_1_node),
    .in16(pull_resistor_2_node), .in17(pull_resistor_3_node), .in18(pull_resistor_4_node),
    .in19(pull_resistor_5_node), .in20(pull_resistor_6_node), .in21(pull_resistor_7_node),
    .in22(pull_resistor_8_node), .in23(pull_resistor_9_node), .in24(pull_resistor_10_node),
    .in25(pull_resistor_11_node), .in26(pull_resistor_12_node), .in27(pull_resistor_13_node),
    .in28(pull_resistor_14_node), .in29(pull_resistor_15_node), .in30(pull_resistor_16_node),
    .in31(pull_resistor_17_node), .out(out_7), .sel(control));
  Register #(.width(32)) register_1 (
    .D(multiplexer_5_out[31:0]), .en(multiplexer_2_out[3]), .Q(register_1_q), .clk(mulclk));  // open: clr
  Register #(.width(32)) register_2 (
    .D(multiplexer_5_out[63:32]), .en(multiplexer_2_out[4]), .Q(register_2_q), .clk(mulclk));  // open: clr
endmodule

module ControlUnit (
  input  [7:0] CompareFlags,
  input  [31:0] Instr,
  output Break,
  output [1:0] RegDst,
  output [1:0] BranchTgt,
  output [1:0] ImmB,
  output [4:0] AluCtl,
  output [4:0] AluShift,
  output RegWrite,
  output MemWrite,
  output MemToReg,
  output SignExt,
  output [1:0] MemLen,
  output AluShiftReg,
  output MemSignExt
);

  wire and_1_out, bitselector_1_out, comparator_1_eq, comparator_2_eq, comparator_3_eq, not_2_out;
  wire [31:0] multiplexer_2_out, multiplexer_3_out, rom_1_data, rom_2_data, rom_3_data;

  Pull_Resistor pull_resistor_1 (.node(RegDst));
  Pull_Resistor pull_resistor_2 (.node(Break));
  not not_1 (Break, comparator_1_eq);
  Comparator #(.mode("unsigned"), .width(2)) comparator_1 (
    .a(multiplexer_3_out[21:20]), .b(2'b00), .eq(comparator_1_eq));  // open: gt, lt
  Multiplexer #(.enable("false"), .width(2)) multiplexer_1 (
    .in0(2'b00), .in1(multiplexer_3_out[5:4]), .out(BranchTgt), .sel(and_1_out));
  Pull_Resistor pull_resistor_3 (.node(BranchTgt));
  Pull_Resistor pull_resistor_4 (.node(ImmB));
  Comparator #(.mode("unsigned"), .width(6)) comparator_2 (
    .a(Instr[31:26]), .b({6{1'b0}}), .eq(comparator_2_eq));  // open: gt, lt
  Comparator #(.mode("unsigned"), .width(6)) comparator_3 (
    .a(Instr[31:26]), .b(6'b000001), .eq(comparator_3_eq));  // open: gt, lt
  and and_1 (and_1_out, multiplexer_3_out[3], bitselector_1_out);
  ROM #(.addrWidth(6), .dataWidth(32)) rom_1 (.addr(Instr[31:26]), .data(rom_1_data));
  ROM #(.addrWidth(6), .dataWidth(32)) rom_2 (.addr(Instr[5:0]), .data(rom_2_data));
  ROM #(.addrWidth(5), .dataWidth(32)) rom_3 (.addr(Instr[20:16]), .data(rom_3_data));
  Pull_Resistor pull_resistor_5 (.node(AluCtl));
  Pull_Resistor pull_resistor_6 (.node(Instr[10:6]));
  Pull_Resistor pull_resistor_7 (.node(RegWrite));
  Multiplexer #(.enable("false"), .width(32)) multiplexer_2 (
    .in0(rom_1_data), .in1(rom_2_data), .out(multiplexer_2_out), .sel(comparator_2_eq));
  Multiplexer #(.enable("false"), .width(32)) multiplexer_3 (
    .in0(multiplexer_2_out), .in1(rom_3_data),
    .out({multiplexer_3_out[31:26], MemSignExt, MemLen, AluShiftReg, multiplexer_3_out[21:20], SignExt, MemToReg, MemWrite, RegWrite, AluCtl, ImmB, multiplexer_3_out[8:3], RegDst, multiplexer_3_out[0]}),
    .sel(comparator_3_eq));
  Pull_Resistor pull_resistor_8 (.node(MemWrite));
  Pull_Resistor pull_resistor_9 (.node(MemToReg));
  not not_2 (not_2_out, multiplexer_3_out[0]);
  LED led_1 (.in(not_2_out));
  BitSelector bitselector_1 (.in(CompareFlags), .out(bitselector_1_out), .sel(multiplexer_3_out[8:6]));

  assign AluShift = Instr[10:6];

  // Notes on the sheet:
  //   I-type conditional jumps
  //   R-type instrs
  //   contents of rom_1 (hex, n*v repeats v):
  //   1a8f800 1a8f800 188647d 189647d 188659d 18865dd 188655d 188649d 1890203 1890203 1891203 1891a03
  //   1812203 1812a03 1813203 1815a03 16*1a8f800 20d0203 28d0203 1a8f800 18d0203 d0203 8d0203 1a8f800
  //   1a8f800 a0201 8a0201 1a8f800 18a0201 20*1a8f800
  //   contents of rom_2 (hex, n*v repeats v):
  //   1894001 1a8f800 1894801 1895001 1c94001 1a8f800 1c94801 1c95001 188646d 189646d 1a8f800 1a8f800
  //   1b8f801 198f801 1a8f800 1a8f800 1897001 1898001 1896801 1897801 4*1a8f800 1898801 1899001 1899801
  //   189a001 4*1a8f800 1890001 1890001 1890801 1890801 1892001 1892801 1893001 1893801 1a8f800 1a8f800
  //   1891001 1891801 20*1a8f800
  //   contents of rom_3 (hex, n*v repeats v):
  //   188651d 18864dd 14*1a8f800 189651d 18964dd 14*1a8f800
  //   I- and J- type instrs
endmodule

module ExeUnit (
  input  DoBreak,
  input  DoResume,
  input  ClkIn,
  input  [31:0] DData,
  input  DValid,
  input  [31:0] IData,
  input  DStall,
  input  IValid,
  output BreakOn,
  output Boot,
  output [31:0] IAddr,
  output DClk,
  output DRead,
  output DWrite,
  output [31:0] DAddr,
  output [31:0] DWrData,
  output [1:0] DLen
);

  wire bwdgate1_1_signalout, clkgen_1_logicstart, clkgen_1_pcreset, clkgen_1_pcupdate,
       controlunit_1_alushiftreg, controlunit_1_break, controlunit_1_memsignext, controlunit_1_regwrite,
       controlunit_1_signext, or_1_out;
  wire [1:0] bwdgate2_1_signalout, controlunit_1_branchtgt, controlunit_1_immb, controlunit_1_regdst;
  wire [4:0] controlunit_1_aluctl, controlunit_1_alushift, fwdgate_1_signalout_2, fwdgate_1_signalout_3,
       multiplexer_4_out, pull_resistor_2_node;
  wire [7:0] comparer_1_compare;
  wire [27:0] adder_1_out;
  wire [31:0] adder_2_out, bwdgate_1_signalout, bwdgate_2_signalout, fwdgate_1_signalout,
       fwdgate_2_signalout, memsigncorrection_1_fixeddata, multiplexer_1_out, multiplexer_2_out,
       multiplexer_3_out, multiplexer_5_out, pull_resistor_1_node, regfile_1_rsval, shifter_1_out,
       signext2_1_extended;
  wire [31:2] bwdgate_3_signalout;
  wire [31:26] bwdgate_3_signalout_2;

  Multiplexer #(.enable("false"), .select(2), .width(32)) multiplexer_1 (
    .in0({bwdgate_3_signalout[31:28], adder_1_out}), .in1(bwdgate_1_signalout), .in2(bwdgate_2_signalout),
    .in3({bwdgate_3_signalout, 2'b00}), .out(multiplexer_1_out), .sel(bwdgate2_1_signalout));
  // Probe on bwdgate2_1_signalout
  D_Flip_Flop d_ff_1 (.Q(BreakOn), .preset(or_1_out), .reset(DoResume));  // open: clk, D, Qn
  LED Logic (.in(clkgen_1_logicstart));
  ClkGen clkgen_1 (
    .PcUpdate(clkgen_1_pcupdate), .Boot(Boot), .PcReset(clkgen_1_pcreset), .LogicStart(clkgen_1_logicstart),
    .LogicEnd(DClk), .ClkDisable(BreakOn), .ClkIn(ClkIn), .MemStall(DStall));
  LED Memory (.in(DClk));
  Multiplexer #(.enable("false"), .width(32)) multiplexer_2 (
    .in0(multiplexer_1_out), .in1(32'h8001fffc), .out(multiplexer_2_out));  // open: sel
  or or_1 (or_1_out, DoBreak, bwdgate1_1_signalout);
  Register #(.width(32)) register_1 (.D(multiplexer_2_out), .Q(IAddr), .clk(clkgen_1_pcupdate));  // open: en, clr
  Adder #(.width(32)) adder_1 (
    .a(IAddr), .b(32'h4), .out({bwdgate_3_signalout[31:28], adder_1_out}));  // open: cin, cout
  LED led_1 (.in(IValid));
  bwdgate1 bwdgate1_1 (.SignalOut(bwdgate1_1_signalout), .Forward(DClk), .SignalIn(controlunit_1_break));
  fwdgate fwdgate_1 (
    .SignalOut({fwdgate_1_signalout[31:21], fwdgate_1_signalout_3, fwdgate_1_signalout_2, fwdgate_1_signalout[10:0]}),
    .SignalIn(IData), .Sample(DClk), .Emit(clkgen_1_logicstart));
  fwdgate fwdgate_2 (
    .SignalOut(fwdgate_2_signalout), .SignalIn({bwdgate_3_signalout[31:28], adder_1_out}), .Sample(DClk),
    .Emit(clkgen_1_logicstart));
  bwdgate2 bwdgate2_1 (.SignalOut(bwdgate2_1_signalout), .Forward(DClk), .SignalIn(controlunit_1_branchtgt));
  bwdgate bwdgate_1 (.SignalOut(bwdgate_1_signalout), .Forward(DClk), .SignalIn(adder_2_out));
  bwdgate bwdgate_2 (.SignalOut(bwdgate_2_signalout), .Forward(DClk), .SignalIn(regfile_1_rsval));
  bwdgate bwdgate_3 (
    .SignalOut({bwdgate_3_signalout_2, bwdgate_3_signalout[27:2]}), .Forward(DClk),
    .SignalIn({fwdgate_1_signalout[31:21], fwdgate_1_signalout_3, fwdgate_1_signalout_2, fwdgate_1_signalout[10:0]}));
  // Probe on fwdgate_1_signalout[25:21]
  // Probe on fwdgate_1_signalout_3
  ControlUnit controlunit_1 (
    .MemWrite(DWrite), .MemToReg(DRead), .SignExt(controlunit_1_signext),
    .AluShiftReg(controlunit_1_alushiftreg), .MemLen(DLen), .MemSignExt(controlunit_1_memsignext),
    .RegDst(controlunit_1_regdst), .Break(controlunit_1_break), .BranchTgt(controlunit_1_branchtgt),
    .ImmB(controlunit_1_immb), .AluCtl(controlunit_1_aluctl), .AluShift(controlunit_1_alushift),
    .RegWrite(controlunit_1_regwrite), .CompareFlags(comparer_1_compare),
    .Instr({fwdgate_1_signalout[31:21], fwdgate_1_signalout_3, fwdgate_1_signalout_2, fwdgate_1_signalout[10:0]}));
  signext2 signext2_1 (
    .Extended(signext2_1_extended), .SignExt(controlunit_1_signext),
    .BitInput({fwdgate_1_signalout_2, fwdgate_1_signalout[10:0]}));
  comparer comparer_1 (.Compare(comparer_1_compare), .Rs(regfile_1_rsval), .Rt(DWrData));
  RegFile regfile_1 (
    .RtVal(DWrData), .RsVal(regfile_1_rsval), .Rs(fwdgate_1_signalout[25:21]), .Rt(fwdgate_1_signalout_3),
    .Rd(multiplexer_4_out), .RdVal(multiplexer_5_out), .WriteEnable(controlunit_1_regwrite), .Clock(DClk));
  Shifter #(.width(32)) shifter_1 (.in(signext2_1_extended), .\dist (5'b00010), .out(shifter_1_out));
  // Probe on controlunit_1_immb
  Pull_Resistor #(.pull("X")) pull_resistor_1 (.node(pull_resistor_1_node));
  Adder #(.width(32)) adder_2 (.a(shifter_1_out), .b(fwdgate_2_signalout), .out(adder_2_out));  // open: cin, cout
  // Probe on regfile_1_rsval
  ALU alu_1 (
    .out_7(DAddr), .A(regfile_1_rsval), .B(multiplexer_3_out), .shamt(controlunit_1_alushift),
    .shamt_reg(controlunit_1_alushiftreg), .control(controlunit_1_aluctl), .mulclk(DClk));
  Multiplexer #(.enable("false"), .select(2), .width(32)) multiplexer_3 (
    .in0(DWrData), .in1(signext2_1_extended), .in2(fwdgate_2_signalout), .in3(pull_resistor_1_node),
    .out(multiplexer_3_out));  // open: sel
  // Probe on controlunit_1_aluctl
  // Probe on multiplexer_3_out
  Pull_Resistor #(.pull("X")) pull_resistor_2 (.node(pull_resistor_2_node));
  // Probe on controlunit_1_regdst
  Multiplexer #(.enable("false"), .select(2), .width(5)) multiplexer_4 (
    .in0(fwdgate_1_signalout_2), .in1(fwdgate_1_signalout_3), .in2({5{1'b1}}), .in3(pull_resistor_2_node),
    .out(multiplexer_4_out));  // open: sel
  // Probe on DAddr
  MemSignCorrection memsigncorrection_1 (
    .FixedData(memsigncorrection_1_fixeddata), .MemData(DData), .AccessLen(DLen),
    .SignExt(controlunit_1_memsignext));
  LED led_2 (.in(DValid));
  // Probe on DRead
  // Probe on multiplexer_5_out
  Multiplexer #(.enable("false"), .width(32)) multiplexer_5 (
    .in0(DAddr), .in1(memsigncorrection_1_fixeddata), .out(multiplexer_5_out), .sel(DRead));
  // Probe on multiplexer_4_out

  // Notes on the sheet:
  //   Clk
  //   PC
  //   IFetch
  //   IDecode
  //   Execute
  //   Memory
  //   WriteBack
endmodule

module RegFile (
  input  Clock,
  input  WriteEnable,
  input  [4:0] Rs,
  input  [4:0] Rt,
  input  [4:0] Rd,
  input  [31:0] RdVal,
  output [31:0] RsVal,
  output [31:0] RtVal
);

  wire [31:0] decoder_1_out0, multiplexer_1_out, multiplexer_2_out, regbank_1_rspick, regbank_1_rtpick,
       regbank_2_rspick, regbank_2_rtpick, regbank_3_rspick, regbank_3_rtpick, regbank_4_rspick,
       regbank_4_rtpick;

  Decoder #(.select(5)) decoder_1 (
    .out0(decoder_1_out0[0]), .out1(decoder_1_out0[1]), .out2(decoder_1_out0[2]), .out3(decoder_1_out0[3]),
    .out4(decoder_1_out0[4]), .out5(decoder_1_out0[5]), .out6(decoder_1_out0[6]), .out7(decoder_1_out0[7]),
    .out8(decoder_1_out0[8]), .out9(decoder_1_out0[9]), .out10(decoder_1_out0[10]),
    .out11(decoder_1_out0[11]), .out12(decoder_1_out0[12]), .out13(decoder_1_out0[13]),
    .out14(decoder_1_out0[14]), .out15(decoder_1_out0[15]), .out16(decoder_1_out0[16]),
    .out17(decoder_1_out0[17]), .out18(decoder_1_out0[18]), .out19(decoder_1_out0[19]),
    .out20(decoder_1_out0[20]), .out21(decoder_1_out0[21]), .out22(decoder_1_out0[22]),
    .out23(decoder_1_out0[23]), .out24(decoder_1_out0[24]), .out25(decoder_1_out0[25]),
    .out26(decoder_1_out0[26]), .out27(decoder_1_out0[27]), .out28(decoder_1_out0[28]),
    .out29(decoder_1_out0[29]), .out30(decoder_1_out0[30]), .out31(decoder_1_out0[31]), .sel(Rd),
    .en(WriteEnable));
  Multiplexer #(.enable("false"), .select(2), .width(32)) multiplexer_1 (
    .in0(regbank_1_rspick), .in1(regbank_2_rspick), .in2(regbank_3_rspick), .in3(regbank_4_rspick),
    .out(multiplexer_1_out), .sel(Rs[4:3]));
  RegBank regbank_1 (
    .RsPick(regbank_1_rspick), .RtPick(regbank_1_rtpick), .Clk(Clock), .RdVal(RdVal),
    .WriteEnable(decoder_1_out0[7:0]), .RsLow(Rs[2:0]), .RtLow(Rt[2:0]));
  RegBank regbank_2 (
    .RsPick(regbank_2_rspick), .RtPick(regbank_2_rtpick), .Clk(Clock), .RdVal(RdVal),
    .WriteEnable(decoder_1_out0[15:8]), .RsLow(Rs[2:0]), .RtLow(Rt[2:0]));
  RegBank regbank_3 (
    .RsPick(regbank_3_rspick), .RtPick(regbank_3_rtpick), .Clk(Clock), .RdVal(RdVal),
    .WriteEnable(decoder_1_out0[23:16]), .RsLow(Rs[2:0]), .RtLow(Rt[2:0]));
  RegBank regbank_4 (
    .RsPick(regbank_4_rspick), .RtPick(regbank_4_rtpick), .Clk(Clock), .RdVal(RdVal),
    .WriteEnable(decoder_1_out0[31:24]), .RsLow(Rs[2:0]), .RtLow(Rt[2:0]));
  Multiplexer #(.enable("false"), .select(2), .width(32)) multiplexer_2 (
    .in0(regbank_1_rtpick), .in1(regbank_2_rtpick), .in2(regbank_3_rtpick), .in3(regbank_4_rtpick),
    .out(multiplexer_2_out), .sel(Rt[4:3]));
  r0_masker r0_masker_1 (.out_3(RsVal), .in_1(Rs), .in_2(multiplexer_1_out));
  r0_masker r0_masker_2 (.out_3(RtVal), .in_1(Rt), .in_2(multiplexer_2_out));
endmodule

module RegBank (
  input  [2:0] RsLow,
  input  [2:0] RtLow,
  input  Clk,
  input  [31:0] RdVal,
  input  [7:0] WriteEnable,
  output [31:0] RsPick,
  output [31:0] RtPick
);

  wire [31:0] register_1_q, register_2_q, register_3_q, register_4_q, register_5_q, register_6_q,
       register_7_q, register_8_q;

  Register #(.width(32)) register_1 (.D(RdVal), .en(WriteEnable[0]), .Q(register_1_q), .clk(Clk));  // open: clr
  Register #(.width(32)) register_2 (.D(RdVal), .en(WriteEnable[1]), .Q(register_2_q), .clk(Clk));  // open: clr
  Register #(.width(32)) register_3 (.D(RdVal), .en(WriteEnable[2]), .Q(register_3_q), .clk(Clk));  // open: clr
  Register #(.width(32)) register_4 (.D(RdVal), .en(WriteEnable[3]), .Q(register_4_q), .clk(Clk));  // open: clr
  Register #(.width(32)) register_5 (.D(RdVal), .en(WriteEnable[4]), .Q(register_5_q), .clk(Clk));  // open: clr
  Register #(.width(32)) register_6 (.D(RdVal), .en(WriteEnable[5]), .Q(register_6_q), .clk(Clk));  // open: clr
  Register #(.width(32)) register_7 (.D(RdVal), .en(WriteEnable[6]), .Q(register_7_q), .clk(Clk));  // open: clr
  Register #(.width(32)) register_8 (.D(RdVal), .en(WriteEnable[7]), .Q(register_8_q), .clk(Clk));  // open: clr
  Multiplexer #(.enable("false"), .select(3), .width(32)) multiplexer_1 (
    .in0(register_1_q), .in1(register_2_q), .in2(register_3_q), .in3(register_4_q), .in4(register_5_q),
    .in5(register_6_q), .in6(register_7_q), .in7(register_8_q), .out(RsPick), .sel(RsLow));
  Multiplexer #(.enable("false"), .select(3), .width(32)) multiplexer_2 (
    .in0(register_1_q), .in1(register_2_q), .in2(register_3_q), .in3(register_4_q), .in4(register_5_q),
    .in5(register_6_q), .in6(register_7_q), .in7(register_8_q), .out(RtPick), .sel(RtLow));
endmodule

module signext2 (
  input  SignExt,
  input  [15:0] BitInput,
  output [31:0] Extended
);

  wire [31:0] bit_extender_1_out, bit_extender_2_out;

  assign bit_extender_1_out = {{16{1'b0}}, BitInput};  // Bit_Extender bit_extender_1
  assign bit_extender_2_out = {{16{BitInput[15]}}, BitInput};  // Bit_Extender bit_extender_2
  Multiplexer #(.enable("false"), .width(32)) multiplexer_1 (
    .in0(bit_extender_1_out), .in1(bit_extender_2_out), .out(Extended), .sel(SignExt));
endmodule

module r0_masker (
  input  [4:0] in_1,
  input  [31:0] in_2,
  output [31:0] out_3
);

  wire comparator_1_eq;

  Comparator #(.width(5)) comparator_1 (.a(in_1), .b({5{1'b0}}), .eq(comparator_1_eq));  // open: gt, lt
  Multiplexer #(.enable("false"), .width(32)) multiplexer_1 (
    .in0(in_2), .in1({32{1'b0}}), .out(out_3), .sel(comparator_1_eq));
endmodule

module comparer (
  input  [31:0] Rs,
  input  [31:0] Rt,
  output [7:0] Compare
);

  not not_1 (Compare[7], Compare[6]);
  not not_2 (Compare[5], Compare[2]);
  Comparator #(.width(32)) comparator_1 (.a(Rs), .b(Rt), .eq(Compare[6]));  // open: gt, lt
  Comparator #(.width(32)) comparator_2 (.a(Rs), .b({32{1'b0}}), .gt(Compare[2]), .lt(Compare[4]));  // open: eq
  not not_3 (Compare[3], Compare[4]);

  assign Compare[1:0] = 2'b10;
endmodule

module ClkGen (
  input  ClkDisable,
  input  ClkIn,
  input  MemStall,
  output Boot,
  output LogicStart,
  output LogicEnd,
  output PcReset,
  output PcUpdate
);

  wire and_1_out, and_2_out, and_3_out, and_5_out, and_6_out, buffer_1_out, d_ff_1_q, d_ff_2_q, d_ff_3_q,
       d_ff_4_q, not_1_out, or_1_out;

  and and_1 (and_1_out, ~ClkDisable, ClkIn);  // AND_Gate
  D_Flip_Flop d_ff_1 (.clk(and_1_out), .D(1'b1), .Q(d_ff_1_q));  // open: Qn, preset, reset
  D_Flip_Flop d_ff_2 (.clk(and_1_out), .D(d_ff_1_q), .Q(d_ff_2_q), .Qn(PcReset));  // open: preset, reset
  and and_2 (and_2_out, d_ff_1_q, PcReset);
  and and_3 (and_3_out, and_1_out, d_ff_3_q);
  or or_1 (or_1_out, and_2_out, and_3_out);
  and and_4 (PcUpdate, or_1_out, ~d_ff_4_q);  // AND_Gate
  D_Flip_Flop d_ff_3 (.clk(and_1_out), .D(d_ff_2_q), .Q(d_ff_3_q), .Qn(Boot));  // open: preset, reset
  and and_5 (and_5_out, d_ff_3_q, buffer_1_out);
  buf buffer_1 (buffer_1_out, and_1_out);
  not not_1 (not_1_out, and_1_out);
  and and_6 (and_6_out, not_1_out, d_ff_3_q);
  Pull_Resistor pull_resistor_1 (.node(MemStall));
  and and_7 (LogicStart, and_5_out, ~d_ff_4_q);  // AND_Gate
  buf buffer_2 (LogicEnd, and_6_out);
  D_Flip_Flop d_ff_4 (.clk(and_6_out), .D(MemStall), .Q(d_ff_4_q));  // open: Qn, preset, reset
endmodule

module fwdgate (
  input  Sample,
  input  Emit,
  input  [31:0] SignalIn,
  output [31:0] SignalOut
);

  wire [31:0] register_1_q;

  Register #(.width(32)) register_1 (.D(SignalIn), .Q(register_1_q), .clk(Sample));  // open: en, clr
  Register #(.width(32)) register_2 (.D(register_1_q), .Q(SignalOut), .clk(Emit));  // open: en, clr
endmodule

module bwdgate (
  input  Forward,
  input  [31:0] SignalIn,
  output [31:0] SignalOut
);

  Register #(.width(32)) register_1 (.D(SignalIn), .Q(SignalOut), .clk(Forward));  // open: en, clr
endmodule

module bwdgate1 (
  input  Forward,
  input  SignalIn,
  output SignalOut
);

  Register #(.width(1)) register_1 (.D(SignalIn), .Q(SignalOut), .clk(Forward));  // open: en, clr
endmodule

module bwdgate2 (
  input  Forward,
  input  [1:0] SignalIn,
  output [1:0] SignalOut
);

  Register #(.width(2)) register_1 (.D(SignalIn), .Q(SignalOut), .clk(Forward));  // open: en, clr
endmodule

module MemGate2 (
  input  InClk,
  input  InRdRq,
  input  InWrRq,
  input  [31:0] InAddr,
  input  [31:0] InWrData,
  input  [31:0] InReadData,
  input  InAddressValid,
  input  InStall,
  input  ParamSub,
  input  [31:0] ParamBase,
  input  [31:0] ParamLen,
  input  ChipValid,
  input  [31:0] ChipRdData,
  input  ChipStall,
  output OutClk,
  output OutRdRq,
  output OutWrRq,
  output [31:0] OutAddr,
  output [31:0] OutWrData,
  output [31:0] OutReadData,
  output OutAddressValid,
  output OutStall,
  output ChipClk,
  output [31:0] ChipWrData,
  output LedRead,
  output [31:0] ChipAddr,
  output ChipRead,
  output LedWrite,
  output ChipWrite
);

  wire and_1_out, and_4_out, comparator_1_lt, comparator_2_lt, not_1_out, or_4_out, pull_resistor_2_node;
  wire [31:0] bit_extender_1_out, pull_resistor_1_node, subtractor_1_out;

  Multiplexer #(.enable("false"), .width(32)) multiplexer_1 (
    .in0(InAddr), .in1(subtractor_1_out), .out(ChipAddr), .sel(ParamSub));
  Comparator #(.mode("unsigned"), .width(32)) comparator_1 (
    .a(InAddr), .b(ParamBase), .lt(comparator_1_lt));  // open: gt, eq
  not not_1 (not_1_out, comparator_1_lt);
  Subtractor #(.width(32)) subtractor_1 (.a(InAddr), .b(ParamBase), .out(subtractor_1_out));  // open: bin, bout
  and and_1 (and_1_out, not_1_out, comparator_2_lt);
  Comparator #(.mode("unsigned"), .width(32)) comparator_2 (
    .a(subtractor_1_out), .b(ParamLen), .lt(comparator_2_lt));  // open: gt, eq
  assign OutReadData = InReadData | pull_resistor_1_node;  // OR_Gate or_1, 32 bits wide
  or or_2 (OutAddressValid, InAddressValid, pull_resistor_2_node);
  or or_3 (OutStall, InStall, and_4_out);
  and and_2 (ChipRead, and_1_out, InRdRq);
  and and_3 (ChipWrite, and_1_out, InWrRq);
  Pull_Resistor pull_resistor_1 (.node(pull_resistor_1_node));
  Pull_Resistor pull_resistor_2 (.node(pull_resistor_2_node));
  and and_4 (and_4_out, or_4_out, ChipStall);
  and and_5 (pull_resistor_2_node, or_4_out, ChipValid);
  or or_4 (or_4_out, ChipRead, ChipWrite);
  Pull_Resistor pull_resistor_3 (.node(ChipStall));
  Pull_Resistor pull_resistor_4 (.node(and_4_out));
  assign pull_resistor_1_node = bit_extender_1_out & ChipRdData;  // AND_Gate and_6, 32 bits wide
  Pull_Resistor pull_resistor_5 (.node(ChipRdData));
  assign bit_extender_1_out = {{31{ChipRead}}, ChipRead};  // Bit_Extender bit_extender_1
  Pull_Resistor pull_resistor_6 (.node(ChipValid));

  assign ChipClk = InClk;
  assign ChipWrData = InWrData;
  assign LedRead = ChipRead;
  assign LedWrite = ChipWrite;
  assign OutAddr = InAddr;
  assign OutClk = InClk;
  assign OutRdRq = InRdRq;
  assign OutWrData = InWrData;
  assign OutWrRq = InWrRq;
endmodule

module AlignmentUnit (
  input  CpuClk,
  input  CpuRd,
  input  CpuWr,
  input  [31:0] CpuAddr,
  input  [31:0] CpuWrData,
  input  [1:0] CpuLen,
  input  [31:0] MemRdData,
  input  MemValid,
  input  MemStall,
  output MemClk,
  output MemRd,
  output MemWr,
  output [31:0] MemAddr,
  output [31:0] MemWrData,
  output [31:0] CpuRdData,
  output CpuValid,
  output CpuStall,
  output UnalignedRead,
  output UnalignedWrite
);

  wire adder_1_cout, and_1_out, and_2_out, and_3_out, and_6_out, and_7_out, and_8_out, and_9_out, and_10_out,
       and_11_out, and_12_out, and_13_out, bwdgate1_1_signalout, bwdgate1_2_signalout, bwdgate1_3_signalout,
       bwdgate1_4_signalout, bwdgate1_5_signalout, bwdgate1_6_signalout, bwdgate1_7_signalout,
       comparator_1_eq, comparator_2_eq, d_ff_1_q, d_ff_1_qn, d_ff_2_q, d_ff_2_qn, d_ff_3_q, d_ff_3_qn,
       d_ff_4_q, d_ff_4_qn, d_ff_5_q, d_ff_5_qn, d_ff_6_q, d_ff_6_qn, d_ff_7_q, d_ff_7_qn, multiplexer_2_out,
       multiplexer_4_out, not_1_out, not_2_out, not_3_out, not_4_out, or_5_out, or_6_out, or_7_out, or_8_out,
       or_9_out, or_10_out, or_11_out;
  wire [1:0] pull_resistor_1_node;
  wire [31:0] adder_2_out, register_1_q, register_2_q, register_3_q, register_4_q;
  wire [63:0] bit_extender_1_out, multiplexer_5_out, writemasker_1_outwindow;

  or or_1 (CpuStall, and_6_out, MemStall, and_11_out);
  Pull_Resistor pull_resistor_1 (.node(pull_resistor_1_node));
  Comparator #(.mode("unsigned"), .width(2)) comparator_1 (
    .a(CpuAddr[1:0]), .b(2'b00), .eq(comparator_1_eq));  // open: gt, lt
  Comparator #(.mode("unsigned"), .width(2)) comparator_2 (
    .a(CpuLen), .b(2'b11), .eq(comparator_2_eq));  // open: gt, lt
  Adder #(.width(2)) adder_1 (.a(CpuAddr[1:0]), .b(CpuLen), .cout(adder_1_cout));  // open: out, cin
  not not_1 (not_1_out, adder_1_cout);
  Multiplexer #(.enable("false"), .width(32)) multiplexer_1 (
    .in0({CpuAddr[31:2], pull_resistor_1_node}), .in1(adder_2_out), .out(MemAddr), .sel(or_8_out));
  Adder #(.width(32)) adder_2 (
    .a({CpuAddr[31:2], pull_resistor_1_node}), .b(32'h4), .out(adder_2_out));  // open: cin, cout
  and and_1 (and_1_out, comparator_1_eq, comparator_2_eq);
  not not_2 (not_2_out, and_1_out);
  and and_2 (and_2_out, and_1_out, CpuRd);
  and and_3 (and_3_out, CpuWr, and_1_out);
  and and_4 (UnalignedRead, not_2_out, CpuRd);
  and and_5 (UnalignedWrite, CpuWr, not_2_out);
  or or_2 (MemRd, and_2_out, and_10_out, or_7_out);
  or or_3 (MemWr, or_6_out, and_3_out);
  or or_4 (CpuValid, MemValid, bwdgate1_5_signalout);
  and and_6 (and_6_out, or_5_out, ~bwdgate1_1_signalout);  // AND_Gate
  or or_5 (or_5_out, bwdgate1_2_signalout, bwdgate1_3_signalout, bwdgate1_4_signalout, d_ff_1_q, UnalignedWrite);
  or or_6 (or_6_out, bwdgate1_2_signalout, bwdgate1_1_signalout);
  or or_7 (or_7_out, bwdgate1_4_signalout, bwdgate1_3_signalout);
  and and_7 (and_7_out, ~bwdgate1_2_signalout, bwdgate1_1_signalout);  // AND_Gate
  bwdgate1 bwdgate1_1 (.SignalOut(bwdgate1_1_signalout), .Forward(not_3_out), .SignalIn(d_ff_4_q));
  bwdgate1 bwdgate1_2 (.SignalOut(bwdgate1_2_signalout), .Forward(not_3_out), .SignalIn(d_ff_3_q));
  bwdgate1 bwdgate1_3 (.SignalOut(bwdgate1_3_signalout), .Forward(not_3_out), .SignalIn(d_ff_2_q));
  bwdgate1 bwdgate1_4 (.SignalOut(bwdgate1_4_signalout), .Forward(not_3_out), .SignalIn(d_ff_1_q));
  not not_3 (not_3_out, and_12_out);
  and and_8 (and_8_out, UnalignedWrite, d_ff_4_qn, d_ff_3_qn, d_ff_2_qn, d_ff_1_qn);
  Register #(.width(32)) register_1 (
    .D(MemRdData), .en(bwdgate1_4_signalout), .Q(register_1_q), .clk(and_12_out));  // open: clr
  Register #(.width(32)) register_2 (
    .D(MemRdData), .en(bwdgate1_3_signalout), .Q(register_2_q), .clk(and_12_out));  // open: clr
  D_Flip_Flop d_ff_1 (.clk(and_12_out), .D(and_8_out), .Q(d_ff_1_q), .Qn(d_ff_1_qn));  // open: preset, reset
  Multiplexer #(.enable("false")) multiplexer_2 (
    .in0(d_ff_1_q), .in1(and_8_out), .out(multiplexer_2_out), .sel(not_1_out));
  or or_8 (or_8_out, bwdgate1_6_signalout, and_7_out);
  WriteMasker writemasker_1 (
    .OutWindow(writemasker_1_outwindow), .WriteLen(CpuLen), .WriteData(CpuWrData), .WriteOff(CpuAddr[1:0]),
    .InWindow({register_2_q, register_1_q}));
  D_Flip_Flop d_ff_2 (.clk(and_12_out), .D(multiplexer_2_out), .Q(d_ff_2_q), .Qn(d_ff_2_qn));  // open: preset, reset
  Multiplexer #(.enable("false"), .width(32)) multiplexer_3 (
    .in0(writemasker_1_outwindow[31:0]), .in1(writemasker_1_outwindow[63:32]), .out(MemWrData),
    .sel(and_7_out));
  D_Flip_Flop d_ff_3 (.clk(and_12_out), .D(d_ff_2_q), .Q(d_ff_3_q), .Qn(d_ff_3_qn));  // open: preset, reset
  Multiplexer #(.enable("false")) multiplexer_4 (
    .in0(d_ff_3_q), .in1(d_ff_2_q), .out(multiplexer_4_out), .sel(not_1_out));
  D_Flip_Flop d_ff_4 (.clk(and_12_out), .D(multiplexer_4_out), .Q(d_ff_4_q), .Qn(d_ff_4_qn));  // open: preset, reset
  and and_9 (and_9_out, ~not_1_out, UnalignedRead);  // AND_Gate
  and and_10 (and_10_out, and_2_out, or_9_out);
  or or_9 (or_9_out, not_1_out, or_10_out);
  and and_11 (and_11_out, or_11_out, ~not_1_out, ~bwdgate1_5_signalout);  // AND_Gate
  or or_10 (or_10_out, bwdgate1_6_signalout, bwdgate1_7_signalout);
  or or_11 (or_11_out, bwdgate1_6_signalout, bwdgate1_7_signalout, d_ff_5_q, and_13_out);
  and and_12 (and_12_out, CpuClk, ~MemStall);  // AND_Gate
  not not_4 (not_4_out, and_12_out);
  and and_13 (and_13_out, and_9_out, d_ff_7_qn, d_ff_6_qn, d_ff_5_qn);
  Register #(.width(32)) register_3 (
    .D(MemRdData), .en(bwdgate1_7_signalout), .Q(register_3_q), .clk(and_12_out));  // open: clr
  Register #(.width(32)) register_4 (
    .D(MemRdData), .en(bwdgate1_6_signalout), .Q(register_4_q), .clk(and_12_out));  // open: clr
  bwdgate1 bwdgate1_5 (.SignalOut(bwdgate1_5_signalout), .Forward(not_4_out), .SignalIn(d_ff_7_q));
  bwdgate1 bwdgate1_6 (.SignalOut(bwdgate1_6_signalout), .Forward(not_4_out), .SignalIn(d_ff_6_q));
  bwdgate1 bwdgate1_7 (.SignalOut(bwdgate1_7_signalout), .Forward(not_4_out), .SignalIn(d_ff_5_q));
  D_Flip_Flop d_ff_5 (.clk(and_12_out), .D(and_13_out), .Q(d_ff_5_q), .Qn(d_ff_5_qn));  // open: preset, reset
  D_Flip_Flop d_ff_6 (.clk(and_12_out), .D(d_ff_5_q), .Q(d_ff_6_q), .Qn(d_ff_6_qn));  // open: preset, reset
  assign bit_extender_1_out = {{32{1'b0}}, MemRdData};  // Bit_Extender bit_extender_1
  Multiplexer #(.enable("false"), .width(64)) multiplexer_5 (
    .in0(bit_extender_1_out), .in1({register_4_q, register_3_q}), .out(multiplexer_5_out),
    .sel(bwdgate1_5_signalout));
  D_Flip_Flop d_ff_7 (.clk(and_12_out), .D(d_ff_6_q), .Q(d_ff_7_q), .Qn(d_ff_7_qn));  // open: preset, reset
  ReadMasker readmasker_1 (.CpuRead(CpuRdData), .ReadLen(CpuLen), .InWindow(multiplexer_5_out), .ReadOff(CpuAddr[1:0]));

  assign MemClk = CpuClk;

  // Notes on the sheet:
  //   Single word fetch
  //   Aligned rd/wr
  //   Unaligned rd/wr
  //   Event detection
  //   Unaligned write engine
  //   Unaligned read engine
endmodule

module ReadMasker (
  input  [1:0] ReadLen,
  input  [63:0] InWindow,
  input  [1:0] ReadOff,
  output [31:0] CpuRead
);

  wire [5:0] multiplexer_2_out;
  wire [31:0] bit_extender_1_out, multiplexer_1_out;
  wire [63:0] shifter_1_out;

  Shifter #(.shift("lr"), .width(64)) shifter_1 (.in(InWindow), .\dist (multiplexer_2_out), .out(shifter_1_out));
  Multiplexer #(.enable("false"), .select(2), .width(32)) multiplexer_1 (
    .in0(32'hff), .in1(32'hffff), .in2(32'hffffff), .in3({32{1'b1}}), .out(multiplexer_1_out));  // open: sel
  Bit_Extender #(.in_width(64), .out_width(32), .\type ("zero")) bit_extender_1 (
    .in(shifter_1_out), .out(bit_extender_1_out));
  Multiplexer #(.enable("false"), .select(2), .width(6)) multiplexer_2 (
    .in0({6{1'b0}}), .in1(6'b001000), .in2(6'b010000), .in3(6'b011000), .out(multiplexer_2_out), .sel(ReadOff));
  assign CpuRead = multiplexer_1_out & bit_extender_1_out;  // AND_Gate and_1, 32 bits wide
endmodule

module WriteMasker (
  input  [63:0] InWindow,
  input  [1:0] WriteLen,
  input  [31:0] WriteData,
  input  [1:0] WriteOff,
  output [63:0] OutWindow
);

  wire [5:0] multiplexer_2_out;
  wire [31:0] multiplexer_1_out;
  wire [63:0] and_1_out, and_2_out, bit_extender_1_out, bit_extender_2_out, shifter_1_out, shifter_2_out;

  Multiplexer #(.enable("false"), .select(2), .width(32)) multiplexer_1 (
    .in0(32'hff), .in1(32'hffff), .in2(32'hffffff), .in3({32{1'b1}}), .out(multiplexer_1_out));  // open: sel
  assign bit_extender_1_out = {{32{1'b0}}, multiplexer_1_out};  // Bit_Extender bit_extender_1
  assign bit_extender_2_out = {{32{1'b0}}, WriteData};  // Bit_Extender bit_extender_2
  Multiplexer #(.enable("false"), .select(2), .width(6)) multiplexer_2 (
    .in0({6{1'b0}}), .in1(6'b001000), .in2(6'b010000), .in3(6'b011000), .out(multiplexer_2_out),
    .sel(WriteOff));
  Shifter #(.width(64)) shifter_1 (.in(bit_extender_1_out), .\dist (multiplexer_2_out), .out(shifter_1_out));
  Shifter #(.width(64)) shifter_2 (.in(bit_extender_2_out), .\dist (multiplexer_2_out), .out(shifter_2_out));
  assign and_1_out = InWindow & ~shifter_1_out;  // AND_Gate and_1, 64 bits wide
  assign and_2_out = shifter_1_out & shifter_2_out;  // AND_Gate and_2, 64 bits wide
  assign OutWindow = and_1_out | and_2_out;  // OR_Gate or_1, 64 bits wide
endmodule

module TtyCtrl (
  input  [31:0] Addr,
  input  Rd,
  input  Wr,
  input  Clk,
  input  [31:0] WrData,
  input  KbdAvail,
  input  [6:0] KbdChar,
  output Stall,
  output Valid,
  output [31:0] RdData,
  output [6:0] LcdChar,
  output LcdClk,
  output LcdReset,
  output LcdEn,
  output KbdClk,
  output KbdEn,
  output KbdReset
);

  wire d_ff_1_q, decoder_1_out1, decoder_1_out2, decoder_1_out3, decoder_2_out0, decoder_2_out1,
       decoder_2_out2, decoder_2_out3, pull_resistor_1_node;
  wire [31:0] bit_extender_1_out, bit_extender_2_out, pull_resistor_9_node, pull_resistor_10_node;

  Pull_Resistor pull_resistor_1 (.node(pull_resistor_1_node));
  Decoder #(.select(2)) decoder_1 (
    .out0(pull_resistor_1_node), .out1(decoder_1_out1), .out2(decoder_1_out2), .out3(decoder_1_out3),
    .sel(Addr[3:2]), .en(Rd));
  Pull_Resistor pull_resistor_2 (.node(decoder_1_out2));
  Pull_Resistor #(.pull("X")) pull_resistor_3 (.node(decoder_1_out3));
  D_Flip_Flop d_ff_1 (.clk(Clk), .D(decoder_1_out1), .Q(d_ff_1_q));  // open: Qn, preset, reset
  and and_1 (KbdClk, ~Clk, d_ff_1_q);  // AND_Gate
  Pull_Resistor #(.pull(1)) pull_resistor_4 (.node(KbdEn));
  Pull_Resistor pull_resistor_5 (.node(Stall));
  Pull_Resistor #(.pull(1)) pull_resistor_6 (.node(Valid));
  Decoder #(.select(2)) decoder_2 (
    .out0(decoder_2_out0), .out1(decoder_2_out1), .out2(decoder_2_out2), .out3(decoder_2_out3),
    .sel(Addr[3:2]), .en(Wr));
  Pull_Resistor pull_resistor_7 (.node(decoder_2_out1));
  Pull_Resistor #(.pull("X")) pull_resistor_8 (.node(decoder_2_out3));
  and and_2 (KbdReset, Clk, decoder_2_out0, WrData[1]);
  Multiplexer #(.select(2), .width(32)) multiplexer_1 (
    .in0(bit_extender_1_out), .in1(bit_extender_2_out), .in2(pull_resistor_9_node),
    .in3(pull_resistor_10_node), .out(RdData));  // open: sel, en
  Pull_Resistor pull_resistor_9 (.node(pull_resistor_9_node));
  Pull_Resistor #(.pull("X")) pull_resistor_10 (.node(pull_resistor_10_node));
  assign bit_extender_1_out = {{31{1'b0}}, KbdAvail};  // Bit_Extender bit_extender_1
  assign bit_extender_2_out = {{25{1'b0}}, KbdChar};  // Bit_Extender bit_extender_2
  Bit_Extender #(.in_width(32), .out_width(7), .\type ("zero")) bit_extender_3 (.in(WrData), .out(LcdChar));
  and and_3 (LcdClk, decoder_2_out2, Clk);
  and and_4 (LcdReset, WrData[2], decoder_2_out0, Clk);
  Pull_Resistor #(.pull(1)) pull_resistor_11 (.node(LcdEn));
endmodule

module LcdCtrl (
  input  [31:0] Addr,
  input  Rd,
  input  Wr,
  input  Clk,
  input  [31:0] WrData,
  output Stall,
  output Valid,
  output [31:0] RdData,
  output [6:0] Xcoord,
  output [6:0] Ycoord,
  output [23:0] Pix,
  output LcdClk,
  output LcdEn,
  output LcdReset
);

  wire bit_extender_2_out, comparator_1_eq, not_1_out;
  wire [23:0] ram_1_dout;
  wire [29:0] subtractor_1_out;
  wire [31:0] bit_extender_4_out;

  Pull_Resistor pull_resistor_1 (.node(Rd));
  Comparator #(.width(30)) comparator_1 (.a(Addr[31:2]), .b({30{1'b0}}), .eq(comparator_1_eq));  // open: gt, lt
  Bit_Extender #(.in_width(30), .out_width(14)) bit_extender_1 (.in(subtractor_1_out), .out({Ycoord, Xcoord}));
  Subtractor #(.width(30)) subtractor_1 (.a(Addr[31:2]), .b(30'h1), .out(subtractor_1_out));  // open: bin, bout
  Pull_Resistor pull_resistor_2 (.node(Stall));
  Pull_Resistor #(.pull(1)) pull_resistor_3 (.node(Valid));
  Multiplexer #(.enable("false"), .width(32)) multiplexer_1 (
    .in0(bit_extender_4_out), .in1({32{1'b0}}), .out(RdData), .sel(comparator_1_eq));
  Bit_Extender #(.in_width(32), .out_width(1), .\type ("zero")) bit_extender_2 (.in(WrData), .out(bit_extender_2_out));
  Bit_Extender #(.in_width(32), .out_width(24), .\type ("zero")) bit_extender_3 (.in(WrData), .out(Pix));
  not not_1 (not_1_out, comparator_1_eq);
  and and_1 (LcdClk, Wr, not_1_out, Clk);
  and and_2 (LcdReset, bit_extender_2_out, comparator_1_eq, Clk);
  Pull_Resistor #(.pull(1)) pull_resistor_4 (.node(LcdEn));
  RAM #(.addrWidth(14), .clearpin("true"), .dataWidth(24), .enables("line")) ram_1 (
    .addr({Ycoord, Xcoord}), .we(LcdEn), .clk(LcdClk), .din(Pix), .dout(ram_1_dout), .clr(LcdReset));
  assign bit_extender_4_out = {{8{1'b0}}, ram_1_dout};  // Bit_Extender bit_extender_4
endmodule

module MemSignCorrection (
  input  SignExt,
  input  [1:0] AccessLen,
  input  [31:0] MemData,
  output [31:0] FixedData
);

  wire [7:0] bit_extender_1_out;
  wire [15:0] bit_extender_3_out;
  wire [31:0] bit_extender_2_out, bit_extender_4_out, multiplexer_2_out, pull_resistor_1_node;

  Bit_Extender #(.in_width(32), .out_width(8)) bit_extender_1 (.in(MemData), .out(bit_extender_1_out));
  assign bit_extender_2_out = {{24{bit_extender_1_out[7]}}, bit_extender_1_out};  // Bit_Extender bit_extender_2
  Bit_Extender #(.in_width(32)) bit_extender_3 (.in(MemData), .out(bit_extender_3_out));
  assign bit_extender_4_out = {{16{bit_extender_3_out[15]}}, bit_extender_3_out};  // Bit_Extender bit_extender_4
  Pull_Resistor #(.pull("X")) pull_resistor_1 (.node(pull_resistor_1_node));
  Multiplexer #(.enable("false"), .width(32)) multiplexer_1 (
    .in0(MemData), .in1(multiplexer_2_out), .out(FixedData), .sel(SignExt));
  Multiplexer #(.enable("false"), .select(2), .width(32)) multiplexer_2 (
    .in0(bit_extender_2_out), .in1(bit_extender_4_out), .in2(pull_resistor_1_node), .in3(MemData),
    .out(multiplexer_2_out), .sel(AccessLen));
endmodule
